# Fritzing sketch DIAGRAMAS (saved by Fritzing 0.8.7b)
breadboards: 1

parts:
  Parte1 = Arduino Uno (Rev3)
  Parte2 = FC-28 Soil Hygrometer Module
  Parte3 = FC-28 Soil Hygrometer Module - Probe
  Parte4 = FC-28 Soil Hygrometer Module - Probe
  Parte5 = FC-28 Soil Hygrometer Module
  M1 = NEO-6M GPS Module [part_number=GY-GPS6MV2]
  Parte6 = DHT22 module

nets:
  N1: Parte1.A0, Parte2.AO
  N2: Parte1.A1, Parte5.AO
  GND: Parte1.GND, Parte2.GND, Parte5.GND, M1.GND, Parte6.GND
  N3: Parte1.D2, M1.Rx
  N4: Parte1.D3_PWM, M1.Tx
  N5: Parte1.D4, Parte6.DATA
  3V3: Parte1.3V3, M1.Vcc
  VCC: Parte1.5V, Parte2.VCC, Parte5.VCC, Parte6.VCC
  N6: Parte2.POS, Parte3.POS
  N7: Parte2.NEG, Parte3.NEG
  N8: Parte4.POS, Parte5.POS
  N9: Parte4.NEG, Parte5.NEG

custom parts:
  FC-28 Soil Hygrometer Module: The FC-28 is a soil hygrometer module that uses the Texas Instruments LM393 comparator chip to provide an analog measurement of soil humidity. The digital output is high when soil moisture is over a certain threshold, as determined by adjusting the potentiometer.
  FC-28 Soil Hygrometer Module - Probe: The FC-28 is a soil hygrometer module that uses the Texas Instruments LM393 comparator chip to provide an analog measurement of soil humidity.
  NEO-6M GPS Module: GY-GPS6MV2 NEO-6M GPS Module Module based on U-blox NEO-6M GPS engine, incorporating regulator for 3.3-5V DC input, MS621FE-compatible rechargeable battery for backup and EEPROM for storing configuration settings. Links: NEO-6 series product information page NEO-6 Datasheet
